# Fritzing sketch diagram (saved by Fritzing 1.0.1rc)
breadboards: 1

parts:
  S1 = Pushbutton [package="[THT]"]
  S2 = Pushbutton [package="[THT]"]
  S3 = Pushbutton [part_number="Power switch" package="[THT]"]
  Mod1 = Raspberry Pi 4B
  LED1 = IR LED - 5mm [package="5 mm [THT]"]
  R1 = Resistor [tolerance=±5% power=0.25W resistance=220 package=THT]

nets:
  N1: S1.Pin_1, S1.Pin_2, S2.Pin_1, S2.Pin_2, S3.Pin_1, S3.Pin_2, Mod1.GND, R1.Pin_0
  N2: S1.Pin_3, S1.Pin_4, Mod1.GPIO17
  N3: S2.Pin_3, S2.Pin_4, Mod1.GPIO18
  N4: S3.Pin_3, S3.Pin_4, Mod1.GPIO21
  N5: Mod1.5V, LED1.anode
  N6: LED1.cathode, R1.Pin_1

custom parts:
  IR LED - 5mm: Black IR led
