# Fritzing sketch shematic (saved by Fritzing 1.0.1rc)
breadboards: 1

parts:
  Mod1 = Raspberry Pi 4B
  LED2 = LED - 5mm [color="Yellow (574nm)" current=0.030A package="5 mm [THT]"]
  R6 = Resistor [tolerance=±5% power=0.25W resistance=330 package=THT]
  S2 = Pushbutton [part_number="preview movie button" package="[THT]"]
  R4 = Resistor [tolerance=±5% power=0.25W resistance=330 package=THT]
  R7 = Resistor [tolerance=±5% power=0.25W resistance=1k package=THT]
  LED6 = LED - 5mm [color="White (4500K)" current=0.030A package="5 mm [THT]"]
  S1 = Pushbutton [part_number="next frame button" package="[THT]"]
  R5 = Resistor [tolerance=±5% power=0.25W resistance=330 package=THT]
  LED4 = LED - 5mm [color="Red (633nm)" current=0.030A package="5 mm [THT]"]
  S3 = Pushbutton [part_number="Power switch" package="[THT]"]
  R9 = Resistor [tolerance=±5% power=0.25W resistance=1k package=THT]
  R10 = Resistor [tolerance=±5% power=0.25W resistance=1k package=THT]
  R3 = Resistor [tolerance=±5% power=0.25W resistance=220 package=THT]
  LED3 = LED - 5mm [color="Green (560nm)" current=0.030A package="5 mm [THT]"]
  R2 = Resistor [tolerance=±5% power=0.25W resistance=330 package=THT]
  LED5 = LED - 5mm [color="Infrared (850nm)" current=0.030A package="5 mm [THT]"]

nets:
  N1: Mod1.5V, LED5.anode
  N2: Mod1.GND, R6.Pin_0, S2.Pin_3, S2.Pin_4, R4.Pin_0, S1.Pin_3, S1.Pin_4, R5.Pin_0, S3.Pin_3, S3.Pin_4, R3.Pin_0, R2.Pin_0
  N3: Mod1.GPIO17, R9.Pin_0
  N4: Mod1.GPIO18, R10.Pin_0
  N5: Mod1.GPIO27, LED2.anode
  N6: Mod1.GPIO22, LED6.anode
  N7: Mod1.GPIO23, LED3.anode
  N8: Mod1.GPIO24, LED4.anode
  N9: Mod1.GPIO21, R7.Pin_0
  N10: LED2.cathode, R2.Pin_1
  N11: R6.Pin_1, LED6.cathode
  N12: S2.Pin_1, S2.Pin_2, R10.Pin_1
  N13: R4.Pin_1, LED3.cathode
  N14: R7.Pin_1, S3.Pin_1, S3.Pin_2
  N15: S1.Pin_1, S1.Pin_2, R9.Pin_1
  N16: R5.Pin_1, LED4.cathode
  N17: R3.Pin_1, LED5.cathode
